// Logisim project GRF.circ as structural Verilog: 2 circuits, main circuit grf
module grf (
  input  CLK,
  input  WE,
  input  reset,
  input  [4:0] A1,
  input  [4:0] A2,
  input  [4:0] A3,
  input  [31:0] WD,
  output [31:0] RD1,
  output [31:0] RD2
);

  wire _0, _1, _2, _3, _4, _5, _6, _7, _8, _9, _10, _11, _12, _13, _14, _15, _16, _17, _18, _19, _20, _21,
       _22, _23, _24, _25, _26, _27, _28, _29, _30, _31;
  wire [31:0] o0, o1, o2, o3, o4, o5, o6, o7, o8, o9, o10, o11, o12, o13, o14, o15, o16, o17, o18, o19, o20,
       o21, o22, o23, o24, o25, o26, o27, o28, o29, o30, o31;

  Decoder #(.select(5)) decoder_1 (
    .out0(_0), .out1(_1), .out2(_2), .out3(_3), .out4(_4), .out5(_5), .out6(_6), .out7(_7), .out8(_8),
    .out9(_9), .out10(_10), .out11(_11), .out12(_12), .out13(_13), .out14(_14), .out15(_15), .out16(_16),
    .out17(_17), .out18(_18), .out19(_19), .out20(_20), .out21(_21), .out22(_22), .out23(_23), .out24(_24),
    .out25(_25), .out26(_26), .out27(_27), .out28(_28), .out29(_29), .out30(_30), .out31(_31), .sel(A3));  // open: en
  // Probe on o0
  rigister rigister_1 (.A3(WD), .sign(_0), .en(1'b0), .CLK(CLK), .reset(reset), .out_6(o0));
  rigister rigister_2 (.A3(WD), .sign(_1), .en(WE), .CLK(CLK), .reset(reset), .out_6(o1));
  rigister rigister_3 (.A3(WD), .sign(_2), .en(WE), .CLK(CLK), .reset(reset), .out_6(o2));
  rigister rigister_4 (.A3(WD), .sign(_3), .en(WE), .CLK(CLK), .reset(reset), .out_6(o3));
  rigister rigister_5 (.A3(WD), .sign(_4), .en(WE), .CLK(CLK), .reset(reset), .out_6(o4));
  rigister rigister_6 (.A3(WD), .sign(_5), .en(WE), .CLK(CLK), .reset(reset), .out_6(o5));
  rigister rigister_7 (.A3(WD), .sign(_6), .en(WE), .CLK(CLK), .reset(reset), .out_6(o6));
  rigister rigister_8 (.A3(WD), .sign(_7), .en(WE), .CLK(CLK), .reset(reset), .out_6(o7));
  rigister rigister_9 (.A3(WD), .sign(_8), .en(WE), .CLK(CLK), .reset(reset), .out_6(o8));
  rigister rigister_10 (.A3(WD), .sign(_9), .en(WE), .CLK(CLK), .reset(reset), .out_6(o9));
  rigister rigister_11 (.A3(WD), .sign(_10), .en(WE), .CLK(CLK), .reset(reset), .out_6(o10));
  rigister rigister_12 (.A3(WD), .sign(_11), .en(WE), .CLK(CLK), .reset(reset), .out_6(o11));
  rigister rigister_13 (.A3(WD), .sign(_12), .en(WE), .CLK(CLK), .reset(reset), .out_6(o12));
  rigister rigister_14 (.A3(WD), .sign(_13), .en(WE), .CLK(CLK), .reset(reset), .out_6(o13));
  rigister rigister_15 (.A3(WD), .sign(_14), .en(WE), .CLK(CLK), .reset(reset), .out_6(o14));
  rigister rigister_16 (.A3(WD), .sign(_15), .en(WE), .CLK(CLK), .reset(reset), .out_6(o15));
  rigister rigister_17 (.A3(WD), .sign(_16), .en(WE), .CLK(CLK), .reset(reset), .out_6(o16));
  rigister rigister_18 (.A3(WD), .sign(_17), .en(WE), .CLK(CLK), .reset(reset), .out_6(o17));
  rigister rigister_19 (.A3(WD), .sign(_18), .en(WE), .CLK(CLK), .reset(reset), .out_6(o18));
  rigister rigister_20 (.A3(WD), .sign(_19), .en(WE), .CLK(CLK), .reset(reset), .out_6(o19));
  rigister rigister_21 (.A3(WD), .sign(_20), .en(WE), .CLK(CLK), .reset(reset), .out_6(o20));
  rigister rigister_22 (.A3(WD), .sign(_21), .en(WE), .CLK(CLK), .reset(reset), .out_6(o21));
  rigister rigister_23 (.A3(WD), .sign(_22), .en(WE), .CLK(CLK), .reset(reset), .out_6(o22));
  rigister rigister_24 (.A3(WD), .sign(_23), .en(WE), .CLK(CLK), .reset(reset), .out_6(o23));
  rigister rigister_25 (.A3(WD), .sign(_24), .en(WE), .CLK(CLK), .reset(reset), .out_6(o24));
  rigister rigister_26 (.A3(WD), .sign(_25), .en(WE), .CLK(CLK), .reset(reset), .out_6(o25));
  rigister rigister_27 (.A3(WD), .sign(_26), .en(WE), .CLK(CLK), .reset(reset), .out_6(o26));
  rigister rigister_28 (.A3(WD), .sign(_27), .en(WE), .CLK(CLK), .reset(reset), .out_6(o27));
  rigister rigister_29 (.A3(WD), .sign(_28), .en(WE), .CLK(CLK), .reset(reset), .out_6(o28));
  rigister rigister_30 (.A3(WD), .sign(_29), .en(WE), .CLK(CLK), .reset(reset), .out_6(o29));
  rigister rigister_31 (.A3(WD), .sign(_30), .en(WE), .CLK(CLK), .reset(reset), .out_6(o30));
  rigister rigister_32 (.A3(WD), .sign(_31), .en(WE), .CLK(CLK), .reset(reset), .out_6(o31));
  Multiplexer #(.select(5), .width(32)) multiplexer_1 (
    .in0(o0), .in1(o1), .in2(o2), .in3(o3), .in4(o4), .in5(o5), .in6(o6), .in7(o7), .in8(o8), .in9(o9),
    .in10(o10), .in11(o11), .in12(o12), .in13(o13), .in14(o14), .in15(o15), .in16(o16), .in17(o17),
    .in18(o18), .in19(o19), .in20(o20), .in21(o21), .in22(o22), .in23(o23), .in24(o24), .in25(o25),
    .in26(o26), .in27(o27), .in28(o28), .in29(o29), .in30(o30), .in31(o31), .out(RD1), .sel(A1));  // open: en
  Multiplexer #(.select(5), .width(32)) multiplexer_2 (
    .in0(o0), .in1(o1), .in2(o2), .in3(o3), .in4(o4), .in5(o5), .in6(o6), .in7(o7), .in8(o8), .in9(o9),
    .in10(o10), .in11(o11), .in12(o12), .in13(o13), .in14(o14), .in15(o15), .in16(o16), .in17(o17),
    .in18(o18), .in19(o19), .in20(o20), .in21(o21), .in22(o22), .in23(o23), .in24(o24), .in25(o25),
    .in26(o26), .in27(o27), .in28(o28), .in29(o29), .in30(o30), .in31(o31), .out(RD2), .sel(A2));  // open: en
endmodule

module rigister (
  input  [31:0] A3,
  input  sign,
  input  reset,
  input  en,
  input  CLK,
  output [31:0] out_6
);

  wire [31:0] multiplexer_1_out;

  Multiplexer #(.width(32)) multiplexer_1 (.in0(out_6), .in1(A3), .out(multiplexer_1_out), .sel(sign));  // open: en
  Register #(.width(32)) register_1 (.D(multiplexer_1_out), .en(en), .Q(out_6), .clk(CLK), .clr(reset));
endmodule
