// Logisim project P0_L0_CRC.circ as structural Verilog: 2 circuits, main circuit CRC
module CRC (
  input  [7:0] in_1,
  input  [3:0] in_2,
  output [10:0] out_3
);

  wire [3:0] mod2_1_out_3, mod2_2_out_3, mod2_3_out_3, mod2_5_out_3, mod2_6_out_3, mod2_7_out_3;
  wire [3:1] mod2_4_out_3;
  wire [3:3] mod2_4_out_3_2, mod2_8_out_3;

  mod2 mod2_1 (.A(in_1[7:4]), .B(in_2), .out_3(mod2_1_out_3));
  mod2 mod2_2 (.A({mod2_1_out_3[2:0], in_1[3]}), .B(in_2), .out_3(mod2_2_out_3));
  mod2 mod2_3 (.A({mod2_2_out_3[2:0], in_1[2]}), .B(in_2), .out_3(mod2_3_out_3));
  mod2 mod2_4 (.A({mod2_3_out_3[2:0], in_1[1]}), .B(in_2), .out_3({mod2_4_out_3_2[3], mod2_4_out_3}));
  mod2 mod2_5 (.A({mod2_4_out_3, in_1[0]}), .B(in_2), .out_3(mod2_5_out_3));
  mod2 mod2_6 (.A({mod2_5_out_3[2:0], 1'b0}), .B(in_2), .out_3(mod2_6_out_3));
  mod2 mod2_7 (.A({mod2_6_out_3[2:0], 1'b0}), .B(in_2), .out_3(mod2_7_out_3));
  mod2 mod2_8 (.A({mod2_7_out_3[2:0], 1'b0}), .B(in_2), .out_3({mod2_8_out_3[3], out_3[2:0]}));

  assign out_3[10:3] = in_1;

  // Other names for the same wires on the sheet: set[7:0] = in_1
endmodule

module mod2 (
  input  [3:0] A,
  input  [3:0] B,
  output [3:0] out_3
);

  wire select;
  wire [3:0] xor_1_out;

  assign xor_1_out = A ^ B;  // XOR_Gate xor_1, 4 bits wide
  Comparator #(.width(1), .mode("unsigned")) comparator_1 (.a(1'b0), .b(A[3]), .eq(select));  // open: gt, lt
  Multiplexer #(.width(4)) multiplexer_1 (.in0(xor_1_out), .in1(A), .out(out_3), .sel(select));  // open: en
endmodule
