// Logisim project P0_L0_FSM.circ as structural Verilog: 3 circuits, main circuit fsm
module fsm (
  input  CLR,
  input  [1:0] In,
  output out_3
);

  wire clock_1_out;
  wire [1:0] multiplexer_1_out, register_1_q, \状态转移_1_n0 ;

  \状态转移  \u_状态转移_1  (
    .s1(register_1_q[1]), .s0(register_1_q[0]), .in1(In[1]), .in0(In[0]), .n1(\状态转移_1_n0 [1]),
    .n0(\状态转移_1_n0 [0]));
  Multiplexer #(.width(2)) multiplexer_1 (
    .in0(\状态转移_1_n0 ), .in1(2'b00), .out(multiplexer_1_out), .sel(CLR));  // open: en
  Clock clock_1 (.out(clock_1_out));
  Register #(.width(2)) register_1 (.D(multiplexer_1_out), .Q(register_1_q), .clk(clock_1_out));  // open: en, clr
  // Probe on nothing
  \状态输出  \u_状态输出_1  (.s1(register_1_q[1]), .s0(register_1_q[0]), .in1(In[1]), .in0(In[0]), .out(out_3));

  // Other names for the same wires on the sheet: re = CLR
endmodule

module \状态转移  (
  input  s1,
  input  s0,
  input  in1,
  input  in0,
  output n1,
  output n0
);

  wire not_1_out, not_2_out, not_3_out;

  not not_1 (not_1_out, s1);
  and and_1 (n1, not_1_out, s0, not_2_out);
  not not_2 (not_2_out, in0);
  not not_3 (not_3_out, in1);
  and and_2 (n0, not_3_out, in0);
endmodule

module \状态输出  (
  input  s1,
  input  s0,
  input  in1,
  input  in0,
  output out
);

  wire not_1_out, not_2_out;

  and and_1 (out, s1, not_1_out, not_2_out);
  not not_1 (not_1_out, s0);
  not not_2 (not_2_out, in0);
endmodule
