// Logisim project P0_L1_ftoi.circ as structural Verilog
module ftoi1 (
  input  [15:0] in_1,
  output [31:0] out_2
);

  wire comparator_1_eq, comparator_1_gt, comparator_2_eq, comparator_3_eq, or_1_out, or_2_out;
  wire [3:0] subtractor_1_out;
  wire [4:0] bit_extender_1_out, bits, subtractor_2_out, subtractor_3_out;
  wire [10:0] out1;
  wire [30:0] out2;
  wire [31:0] sum, \补码_1_out_2 ;
  wire [31:31] shifter_2_out;

  Subtractor #(.width(4)) subtractor_1 (.a(4'b1010), .b(bits[3:0]), .out(subtractor_1_out));  // open: bin, bout
  // Probe on subtractor_1_out
  Comparator #(.width(4), .mode("unsigned")) comparator_1 (
    .a(4'b1010), .b(bits[3:0]), .gt(comparator_1_gt), .eq(comparator_1_eq));  // open: lt
  // Probe on bit_extender_1_out
  // Probe on in_1[14:10]
  // Probe on 5'b01111
  or or_1 (or_1_out, comparator_1_gt, comparator_1_eq);
  assign bit_extender_1_out = {{1{1'b0}}, bits[3:0]};  // Bit_Extender bit_extender_1
  Shifter #(.width(11), .shift("lr")) shifter_1 (.in({1'b1, in_1[9:0]}), .\dist (subtractor_1_out), .out(out1));
  // Probe on out1
  Subtractor #(.width(5)) subtractor_2 (
    .a(bit_extender_1_out), .b(5'b01010), .out(subtractor_2_out));  // open: bin, bout
  // Probe on bits
  Subtractor #(.width(5)) subtractor_3 (.a(in_1[14:10]), .b(5'b01111), .out(subtractor_3_out));  // open: bin, bout
  // Probe on subtractor_2_out
  \tran  tran_1 (.in_1(subtractor_3_out), .out_2(bits));
  Shifter #(.width(32)) shifter_2 (.in({22'h1, in_1[9:0]}), .\dist (subtractor_2_out), .out({shifter_2_out[31], out2}));
  Multiplexer #(.width(32)) multiplexer_1 (
    .in0({in_1[15], out2}), .in1({in_1[15], {20{1'b0}}, out1}), .out(sum), .sel(or_1_out));  // open: en
  \补码  \u_补码_1  (.in_1(sum), .out_2(\补码_1_out_2 ));
  Comparator #(.width(5), .mode("unsigned")) comparator_2 (
    .a({5{1'b1}}), .b(in_1[14:10]), .eq(comparator_2_eq));  // open: gt, lt
  Comparator #(.width(5), .mode("unsigned")) comparator_3 (
    .a({5{1'b0}}), .b(in_1[14:10]), .eq(comparator_3_eq));  // open: gt, lt
  or or_2 (or_2_out, comparator_2_eq, comparator_3_eq, bits[4]);
  Multiplexer #(.width(32)) multiplexer_2 (
    .in0(\补码_1_out_2 ), .in1({32{1'b0}}), .out(out_2), .sel(or_2_out));  // open: en

  // Other names for the same wires on the sheet: frac[9:0] = in_1[9:0]; out[3:0] = bits[3:0];
  //   exponent[4:0] = in_1[14:10]; out1[31] = in_1[15]; out2[31] = in_1[15]; sign = in_1[15]
endmodule

module \补码  (
  input  [31:0] in_1,
  output [31:0] out_2
);

  wire comparator_1_eq;
  wire [30:0] adder_1_out, not_1_out;

  assign not_1_out = ~in_1[30:0];  // NOT_Gate not_1, 31 bits wide
  Comparator #(.width(1), .mode("unsigned")) comparator_1 (
    .a(1'b1), .b(in_1[31]), .eq(comparator_1_eq));  // open: gt, lt
  Adder #(.width(31)) adder_1 (.a(31'h1), .b(not_1_out), .out(adder_1_out));  // open: cin, cout
  Multiplexer #(.width(32)) multiplexer_1 (
    .in0(in_1), .in1({in_1[31], adder_1_out}), .out(out_2), .sel(comparator_1_eq));  // open: en
endmodule

module \tran  (
  input  [4:0] in_1,
  output [4:0] out_2
);

  wire and_1_out;
  wire [3:0] adder_1_out, not_1_out;

  assign not_1_out = ~in_1[3:0];  // NOT_Gate not_1, 4 bits wide
  and and_1 (and_1_out, 1'b1, in_1[4]);
  Adder #(.width(4)) adder_1 (.a(4'b0001), .b(not_1_out), .out(adder_1_out));  // open: cin, cout
  Multiplexer #(.width(5)) multiplexer_1 (
    .in0(in_1), .in1({in_1[4], adder_1_out}), .out(out_2), .sel(and_1_out));  // open: en
endmodule

module _1 (
  input  [4:0] in_1
);

  wire [4:0] bits;

  // Probe on in_1
  // Probe on 5'b01111
  // Probe on bits
  Subtractor #(.width(5)) subtractor_1 (.a(in_1), .b(5'b01111), .out(bits));  // open: bin, bout
endmodule

module ftoi (
  input  [15:0] in_1,
  output [31:0] out_2
);

  wire comparator_1_eq, comparator_2_eq, or_1_out;
  wire [4:0] bits, subtractor_1_out;
  wire [31:0] bit_extender_1_out, shifter_1_out, sum, undriven;

  // Probe on in_1[14:10]
  // Probe on 5'b01111
  assign bit_extender_1_out = {{21{1'b0}}, {1'b1, in_1[9:0]}};  // Bit_Extender bit_extender_1
  // Probe on bits
  Subtractor #(.width(5)) subtractor_1 (.a(in_1[14:10]), .b(5'b01111), .out(subtractor_1_out));  // open: bin, bout
  Shifter #(.width(32)) shifter_1 (.in(bit_extender_1_out), .\dist ({1'b0, bits[3:0]}), .out(shifter_1_out));
  \tran  tran_1 (.in_1(subtractor_1_out), .out_2(bits));
  Shifter #(.width(32), .shift("lr")) shifter_2 (.in(shifter_1_out), .\dist (5'b01010), .out(sum));
  Comparator #(.width(5), .mode("unsigned")) comparator_1 (
    .a({5{1'b1}}), .b(in_1[14:10]), .eq(comparator_1_eq));  // open: gt, lt
  Comparator #(.width(5), .mode("unsigned")) comparator_2 (
    .a({5{1'b0}}), .b(in_1[14:10]), .eq(comparator_2_eq));  // open: gt, lt
  or or_1 (or_1_out, comparator_1_eq, comparator_2_eq, bits[4]);
  Multiplexer #(.width(32)) multiplexer_1 (.in0(undriven), .in1({32{1'b0}}), .out(out_2), .sel(or_1_out));  // open: en

  // Other names for the same wires on the sheet: frac[9:0] = in_1[9:0]; out[3:0] = bits[3:0]; shift[3:0] = bits[3:0];
  //   exponent[4:0] = in_1[14:10]; sign = in_1[15]
endmodule
