// Logisim project P0_L1_navigation_2020.circ as structural Verilog: 5 circuits, main circuit navigation
module navigation (
  input  [1:0] dir,
  input  clk,
  input  reset,
  output arrive,
  output hit
);

  wire \状态转移_1_hit ;
  wire [2:0] register_1_q, \状态转移_1_next0 ;

  \状态转移  \u_状态转移_1  (
    .s2(register_1_q[2]), .s1(register_1_q[1]), .s0(register_1_q[0]), .dir1(dir[1]), .dir0(dir[0]),
    .next2(\状态转移_1_next0 [2]), .next1(\状态转移_1_next0 [1]), .next0(\状态转移_1_next0 [0]), .hit(\状态转移_1_hit ));
  Register #(.width(3)) register_1 (.D(\状态转移_1_next0 ), .Q(register_1_q), .clk(clk), .clr(reset));  // open: en
  Register #(.width(1)) register_2 (.D(\状态转移_1_hit ), .Q(hit), .clk(clk), .clr(reset));  // open: en
  \状态输出  \u_状态输出_1  (.s2(register_1_q[2]), .s1(register_1_q[1]), .s0(register_1_q[0]), .out(arrive));
endmodule

module \状态转移  (
  input  s2,
  input  s1,
  input  s0,
  input  dir1,
  input  dir0,
  output next2,
  output next1,
  output next0,
  output hit
);

  wire and_1_out, and_2_out, and_3_out, and_4_out, and_5_out, and_6_out, and_7_out, and_8_out, and_9_out,
       and_10_out, and_11_out, and_12_out, and_13_out, and_14_out, and_15_out, and_16_out, not_1_out,
       not_2_out, not_3_out, not_4_out, not_5_out, not_6_out, not_7_out, not_8_out, not_9_out, not_10_out,
       not_11_out, not_12_out, not_13_out, not_14_out, not_15_out, not_16_out, not_17_out, not_18_out,
       not_19_out, not_20_out, not_21_out, not_22_out, not_23_out, not_24_out, not_25_out, not_26_out,
       not_27_out, not_28_out, not_29_out, not_30_out, not_31_out, not_32_out, not_33_out, not_34_out,
       not_35_out, not_36_out, not_37_out, not_38_out, not_39_out, not_40_out;

  not not_1 (not_1_out, s2);
  not not_2 (not_2_out, s0);
  not not_3 (not_3_out, dir1);
  not not_4 (not_4_out, dir0);
  not not_5 (not_5_out, s2);
  not not_6 (not_6_out, dir1);
  not not_7 (not_7_out, s2);
  not not_8 (not_8_out, s1);
  not not_9 (not_9_out, dir1);
  not not_10 (not_10_out, s2);
  not not_11 (not_11_out, dir1);
  not not_12 (not_12_out, dir0);
  not not_13 (not_13_out, s2);
  not not_14 (not_14_out, s0);
  not not_15 (not_15_out, dir1);
  not not_16 (not_16_out, s2);
  not not_17 (not_17_out, s0);
  not not_18 (not_18_out, dir0);
  not not_19 (not_19_out, s2);
  not not_20 (not_20_out, s2);
  not not_21 (not_21_out, s1);
  not not_22 (not_22_out, dir1);
  not not_23 (not_23_out, dir0);
  not not_24 (not_24_out, s2);
  not not_25 (not_25_out, s2);
  not not_26 (not_26_out, s2);
  not not_27 (not_27_out, dir0);
  not not_28 (not_28_out, s2);
  not not_29 (not_29_out, s0);
  not not_30 (not_30_out, dir1);
  not not_31 (not_31_out, s2);
  not not_32 (not_32_out, s1);
  not not_33 (not_33_out, s0);
  not not_34 (not_34_out, s2);
  not not_35 (not_35_out, s0);
  not not_36 (not_36_out, dir0);
  not not_37 (not_37_out, s2);
  not not_38 (not_38_out, s2);
  not not_39 (not_39_out, dir1);
  not not_40 (not_40_out, dir0);
  and and_1 (and_1_out, not_1_out, s1, not_2_out, not_3_out, not_4_out);
  and and_2 (and_2_out, not_5_out, s1, s0, not_6_out, dir0);
  and and_3 (and_3_out, not_7_out, not_8_out, s0, not_9_out);
  and and_4 (and_4_out, not_10_out, s0, not_11_out, not_12_out);
  and and_5 (and_5_out, not_13_out, s1, not_14_out, not_15_out, dir0);
  and and_6 (and_6_out, not_16_out, s1, not_17_out, dir1, not_18_out);
  and and_7 (and_7_out, not_19_out, s1, s0, dir1, dir0);
  and and_8 (and_8_out, not_20_out, not_21_out, not_22_out, not_23_out);
  and and_9 (and_9_out, not_24_out, s0, dir1, dir0);
  and and_10 (and_10_out, not_25_out, s1, dir1, dir0);
  and and_11 (and_11_out, not_26_out, s1, s0, not_27_out);
  and and_12 (and_12_out, not_28_out, not_29_out, not_30_out, dir0);
  and and_13 (and_13_out, not_31_out, not_32_out, not_33_out, dir1);
  and and_14 (and_14_out, not_34_out, not_35_out, dir1, not_36_out);
  and and_15 (and_15_out, not_37_out, s0, dir1, dir0);
  and and_16 (and_16_out, not_38_out, s1, s0, not_39_out, not_40_out);
  or or_1 (next2, and_1_out, and_2_out);
  or or_2 (next1, and_3_out, and_4_out, and_5_out, and_6_out, and_7_out);
  or or_3 (next0, and_8_out, and_9_out, and_10_out, and_11_out);
  or or_4 (hit, and_12_out, and_13_out, and_14_out, and_15_out, and_16_out);
endmodule

module \状态输出  (
  input  s2,
  input  s1,
  input  s0,
  output out
);

  wire not_1_out, not_2_out;

  not not_1 (not_1_out, s1);
  not not_2 (not_2_out, s0);
  and and_1 (out, s2, not_1_out, not_2_out);
endmodule

module hit_out (
  input  s2,
  input  s1,
  input  s0,
  input  dir1,
  input  dir0,
  output hit
);

  wire and_1_out, and_2_out, and_3_out, and_4_out, and_5_out, not_1_out, not_2_out, not_3_out, not_4_out,
       not_5_out, not_6_out, not_7_out, not_8_out, not_9_out, not_10_out, not_11_out, not_12_out, not_13_out;

  not not_1 (not_1_out, s2);
  not not_2 (not_2_out, s0);
  not not_3 (not_3_out, dir1);
  not not_4 (not_4_out, s2);
  not not_5 (not_5_out, s1);
  not not_6 (not_6_out, s0);
  not not_7 (not_7_out, s2);
  not not_8 (not_8_out, s0);
  not not_9 (not_9_out, dir0);
  not not_10 (not_10_out, s2);
  not not_11 (not_11_out, s2);
  not not_12 (not_12_out, dir1);
  not not_13 (not_13_out, dir0);
  and and_1 (and_1_out, not_1_out, not_2_out, not_3_out, dir0);
  and and_2 (and_2_out, not_4_out, not_5_out, not_6_out, dir1);
  and and_3 (and_3_out, not_7_out, not_8_out, dir1, not_9_out);
  and and_4 (and_4_out, not_10_out, s0, dir1, dir0);
  and and_5 (and_5_out, not_11_out, s1, s0, not_12_out, not_13_out);
  or or_1 (hit, and_1_out, and_2_out, and_3_out, and_4_out, and_5_out);
endmodule

module navigation2 (
  input  [1:0] dir,
  input  clk,
  input  reset,
  output arrive,
  output hit
);

  wire [2:0] register_1_q, register_2_q, \状态转移_1_next0 ;

  \状态转移  \u_状态转移_1  (
    .s2(register_1_q[2]), .s1(register_1_q[1]), .s0(register_1_q[0]), .dir1(dir[1]), .dir0(dir[0]),
    .next2(\状态转移_1_next0 [2]), .next1(\状态转移_1_next0 [1]), .next0(\状态转移_1_next0 [0]));  // open: hit
  Register #(.width(3)) register_1 (.D(\状态转移_1_next0 ), .Q(register_1_q), .clk(clk), .clr(reset));  // open: en
  \状态输出  \u_状态输出_1  (.s2(register_1_q[2]), .s1(register_1_q[1]), .s0(register_1_q[0]), .out(arrive));
  Register #(.width(3)) register_2 (.D(\状态转移_1_next0 ), .Q(register_2_q), .clk(clk), .clr(reset));  // open: en
  \状态转移  \u_状态转移_2  (
    .s2(register_2_q[2]), .s1(register_2_q[1]), .s0(register_2_q[0]), .dir1(dir[1]), .dir0(dir[0]),
    .next0(hit));  // open: next2, next1, hit
endmodule
