// Logisim project cpu.circ as structural Verilog: 9 circuits, main circuit main
module GRF (
  input  CLK,
  input  WE,
  input  reset,
  input  [4:0] A1,
  input  [4:0] A2,
  input  [4:0] A3,
  input  [31:0] WD,
  output [31:0] RD1,
  output [31:0] RD2
);

  wire _0, _1, _2, _3, _4, _5, _6, _7, _8, _9, _10, _11, _12, _13, _14, _15, _16, _17, _18, _19, _20, _21,
       _22, _23, _24, _25, _26, _27, _28, _29, _30, _31;
  wire [31:0] o0, o1, o2, o3, o4, o5, o6, o7, o8, o9, o10, o11, o12, o13, o14, o15, o16, o17, o18, o19, o20,
       o21, o22, o23, o24, o25, o26, o27, o28, o29, o30, o31;

  // Probe on o0
  Decoder #(.select(5)) decoder_1 (
    .out0(_0), .out1(_1), .out2(_2), .out3(_3), .out4(_4), .out5(_5), .out6(_6), .out7(_7), .out8(_8),
    .out9(_9), .out10(_10), .out11(_11), .out12(_12), .out13(_13), .out14(_14), .out15(_15), .out16(_16),
    .out17(_17), .out18(_18), .out19(_19), .out20(_20), .out21(_21), .out22(_22), .out23(_23), .out24(_24),
    .out25(_25), .out26(_26), .out27(_27), .out28(_28), .out29(_29), .out30(_30), .out31(_31), .sel(A3));  // open: en
  rigister rigister_1 (.A3(WD), .sign(_0), .en(1'b0), .CLK(CLK), .reset(reset), .out_6(o0));
  rigister rigister_2 (.A3(WD), .sign(_1), .en(WE), .CLK(CLK), .reset(reset), .out_6(o1));
  rigister rigister_3 (.A3(WD), .sign(_2), .en(WE), .CLK(CLK), .reset(reset), .out_6(o2));
  rigister rigister_4 (.A3(WD), .sign(_3), .en(WE), .CLK(CLK), .reset(reset), .out_6(o3));
  rigister rigister_5 (.A3(WD), .sign(_4), .en(WE), .CLK(CLK), .reset(reset), .out_6(o4));
  rigister rigister_6 (.A3(WD), .sign(_5), .en(WE), .CLK(CLK), .reset(reset), .out_6(o5));
  rigister rigister_7 (.A3(WD), .sign(_6), .en(WE), .CLK(CLK), .reset(reset), .out_6(o6));
  rigister rigister_8 (.A3(WD), .sign(_7), .en(WE), .CLK(CLK), .reset(reset), .out_6(o7));
  rigister rigister_9 (.A3(WD), .sign(_8), .en(WE), .CLK(CLK), .reset(reset), .out_6(o8));
  rigister rigister_10 (.A3(WD), .sign(_9), .en(WE), .CLK(CLK), .reset(reset), .out_6(o9));
  rigister rigister_11 (.A3(WD), .sign(_10), .en(WE), .CLK(CLK), .reset(reset), .out_6(o10));
  rigister rigister_12 (.A3(WD), .sign(_11), .en(WE), .CLK(CLK), .reset(reset), .out_6(o11));
  rigister rigister_13 (.A3(WD), .sign(_12), .en(WE), .CLK(CLK), .reset(reset), .out_6(o12));
  rigister rigister_14 (.A3(WD), .sign(_13), .en(WE), .CLK(CLK), .reset(reset), .out_6(o13));
  rigister rigister_15 (.A3(WD), .sign(_14), .en(WE), .CLK(CLK), .reset(reset), .out_6(o14));
  rigister rigister_16 (.A3(WD), .sign(_15), .en(WE), .CLK(CLK), .reset(reset), .out_6(o15));
  rigister rigister_17 (.A3(WD), .sign(_16), .en(WE), .CLK(CLK), .reset(reset), .out_6(o16));
  rigister rigister_18 (.A3(WD), .sign(_17), .en(WE), .CLK(CLK), .reset(reset), .out_6(o17));
  rigister rigister_19 (.A3(WD), .sign(_18), .en(WE), .CLK(CLK), .reset(reset), .out_6(o18));
  rigister rigister_20 (.A3(WD), .sign(_19), .en(WE), .CLK(CLK), .reset(reset), .out_6(o19));
  rigister rigister_21 (.A3(WD), .sign(_20), .en(WE), .CLK(CLK), .reset(reset), .out_6(o20));
  rigister rigister_22 (.A3(WD), .sign(_21), .en(WE), .CLK(CLK), .reset(reset), .out_6(o21));
  rigister rigister_23 (.A3(WD), .sign(_22), .en(WE), .CLK(CLK), .reset(reset), .out_6(o22));
  rigister rigister_24 (.A3(WD), .sign(_23), .en(WE), .CLK(CLK), .reset(reset), .out_6(o23));
  rigister rigister_25 (.A3(WD), .sign(_24), .en(WE), .CLK(CLK), .reset(reset), .out_6(o24));
  rigister rigister_26 (.A3(WD), .sign(_25), .en(WE), .CLK(CLK), .reset(reset), .out_6(o25));
  rigister rigister_27 (.A3(WD), .sign(_26), .en(WE), .CLK(CLK), .reset(reset), .out_6(o26));
  rigister rigister_28 (.A3(WD), .sign(_27), .en(WE), .CLK(CLK), .reset(reset), .out_6(o27));
  rigister rigister_29 (.A3(WD), .sign(_28), .en(WE), .CLK(CLK), .reset(reset), .out_6(o28));
  rigister rigister_30 (.A3(WD), .sign(_29), .en(WE), .CLK(CLK), .reset(reset), .out_6(o29));
  rigister rigister_31 (.A3(WD), .sign(_30), .en(WE), .CLK(CLK), .reset(reset), .out_6(o30));
  rigister rigister_32 (.A3(WD), .sign(_31), .en(WE), .CLK(CLK), .reset(reset), .out_6(o31));
  Multiplexer #(.select(5), .width(32)) multiplexer_1 (
    .in0(o0), .in1(o1), .in2(o2), .in3(o3), .in4(o4), .in5(o5), .in6(o6), .in7(o7), .in8(o8), .in9(o9),
    .in10(o10), .in11(o11), .in12(o12), .in13(o13), .in14(o14), .in15(o15), .in16(o16), .in17(o17),
    .in18(o18), .in19(o19), .in20(o20), .in21(o21), .in22(o22), .in23(o23), .in24(o24), .in25(o25),
    .in26(o26), .in27(o27), .in28(o28), .in29(o29), .in30(o30), .in31(o31), .out(RD2), .sel(A2));  // open: en
  Multiplexer #(.select(5), .width(32)) multiplexer_2 (
    .in0(o0), .in1(o1), .in2(o2), .in3(o3), .in4(o4), .in5(o5), .in6(o6), .in7(o7), .in8(o8), .in9(o9),
    .in10(o10), .in11(o11), .in12(o12), .in13(o13), .in14(o14), .in15(o15), .in16(o16), .in17(o17),
    .in18(o18), .in19(o19), .in20(o20), .in21(o21), .in22(o22), .in23(o23), .in24(o24), .in25(o25),
    .in26(o26), .in27(o27), .in28(o28), .in29(o29), .in30(o30), .in31(o31), .out(RD1), .sel(A1));  // open: en
endmodule

module rigister (
  input  [31:0] A3,
  input  sign,
  input  reset,
  input  en,
  input  CLK,
  output [31:0] out_6
);

  wire [31:0] multiplexer_1_out;

  Multiplexer #(.width(32)) multiplexer_1 (.in0(out_6), .in1(A3), .out(multiplexer_1_out), .sel(sign));  // open: en
  Register #(.width(32)) register_1 (.D(multiplexer_1_out), .en(en), .Q(out_6), .clk(CLK), .clr(reset));
endmodule

module IM (
  input  [4:0] A,
  output [31:0] D
);

  ROM #(.addrWidth(5), .dataWidth(32)) rom_1 (.addr(A), .data(D));  // open: sel

  // Notes on the sheet:
  //   contents of rom_1 (hex, n*v repeats v):
  //   3c000064
endmodule

module main (
  input  reset,
  output [31:0] Instr,
  output RegWrite,
  output [4:0] RegAddr,
  output [31:0] RegData,
  output MemWrite,
  output [4:0] MemAddr,
  output [31:0] MemData
);

  wire Alu_2_t, and_1_out, Branch, clk, Extop, lui, MemRead, or_1_out, RegDst, RegRead, sw, zero;
  wire [1:1] not_1_out;
  wire [2:0] ALU_control;
  wire [4:0] multiplexer_1_out, multiplexer_3_out;
  wire [31:0] ALU_1, ALU_2, dm_1_rd, ext_1_result, ext_2_result, MD, multiplexer_4_out, result;

  ext ext_1 (.imm_16(Instr[15:0]), .extop(Extop), .result(ext_1_result));
  Multiplexer #(.width(5)) multiplexer_1 (
    .in0({5{1'b0}}), .in1(Instr[20:16]), .out(multiplexer_1_out), .sel(RegRead));  // open: en
  Multiplexer #(.select(2), .width(5)) multiplexer_2 (
    .in0(Instr[20:16]), .in1(Instr[15:11]), .in2({5{1'b0}}), .in3({5{1'b0}}), .out(RegAddr),
    .sel({not_1_out[1], RegDst}));  // open: en
  not not_1 (not_1_out[1], RegWrite);
  and and_1 (and_1_out, Branch, zero);
  // Probe on multiplexer_1_out
  Multiplexer #(.width(5)) multiplexer_3 (
    .in0(Instr[25:21]), .in1({5{1'b0}}), .out(multiplexer_3_out), .sel(lui));  // open: en
  // Probe on RegAddr
  IFU ifu_1 (.clk(clk), .reset(reset), .imm(ext_1_result), .Branch(and_1_out), .instr(Instr));
  // Probe on multiplexer_3_out
  GRF grf_1 (
    .A1(multiplexer_3_out), .A2(multiplexer_1_out), .A3(RegAddr), .WD(RegData), .CLK(clk), .reset(reset),
    .WE(RegWrite), .RD1(ALU_1), .RD2(MD));
  Clock clock_1 (.out(clk));
  // Probe on Instr
  // Probe on ALU_1
  // Probe on MD
  ext ext_2 (.imm_16(Instr[15:0]), .extop(Extop), .result(ext_2_result));
  Multiplexer #(.width(32)) multiplexer_4 (
    .in0(ext_2_result), .in1({Instr[15:0], {16{1'b0}}}), .out(multiplexer_4_out), .sel(lui));  // open: en
  // Probe on ALU_2
  Multiplexer #(.width(32)) multiplexer_5 (.in0(MD), .in1(multiplexer_4_out), .out(ALU_2), .sel(Alu_2_t));  // open: en
  ALU u_alu_1 (.A1(ALU_1), .A2(ALU_2), .ALU_control(ALU_control), .out(result), .zero(zero));
  // Probe on ALU_control
  // Probe on result
  Controller controller_1 (
    .opcode(Instr[31:26]), .func(Instr[5:0]), .RegRead_2(RegRead), .RegWrite(RegWrite), .extop(Extop),
    .MemWrite(MemWrite), .RegRead_1(lui), .Alu_2(Alu_2_t), .MemRead(MemRead), .Branch(Branch),
    .Alu_control(ALU_control), .RegDst(RegDst), .sw(sw));
  // Probe on MD
  Multiplexer #(.width(32)) multiplexer_6 (.in0({32{1'b0}}), .in1(MD), .out(MemData), .sel(MemWrite));  // open: en
  or or_1 (or_1_out, MemRead, MemWrite);
  Multiplexer #(.width(5)) multiplexer_7 (
    .in0({5{1'b0}}), .in1(result[6:2]), .out(MemAddr), .sel(or_1_out));  // open: en
  // Probe on MemAddr
  DM dm_1 (.A(MemAddr), .WD(MemData), .WE(MemWrite), .clk(clk), .MemRead(MemRead), .RD(dm_1_rd), .reset(reset));
  // Probe on dm_1_rd
  Multiplexer #(.width(32)) multiplexer_8 (.in0(result), .in1(dm_1_rd), .out(RegData), .sel(MemRead));  // open: en
  // Probe on RegData

  // Other names for the same wires on the sheet: func[5:0] = Instr[5:0]; imm_16[15:0] = Instr[15:0];
  //   imm_26[25:0] = Instr[25:0]; opcode[5:0] = Instr[31:26]; rd[4:0] = Instr[15:11]; rs[4:0] = Instr[25:21];
  //   rt[4:0] = Instr[20:16]; shamt[4:0] = Instr[10:6]; WD[31:0] = RegData
endmodule

module IFU (
  input  clk,
  input  reset,
  input  [31:0] imm,
  input  Branch,
  output [31:0] instr
);

  wire [31:0] adder_1_out, adder_2_out, multiplexer_1_out, PC_q, shifter_1_out;

  Register #(.width(32)) PC (.D(multiplexer_1_out), .Q(PC_q), .clk(clk), .clr(reset));  // open: en
  Shifter #(.width(32)) shifter_1 (.in(imm), .\dist (5'b00010), .out(shifter_1_out));
  Adder #(.width(32)) adder_1 (.a(PC_q), .b(32'h4), .out(adder_1_out));  // open: cin, cout
  IM im_1 (.A(PC_q[6:2]), .D(instr));
  Adder #(.width(32)) adder_2 (.a(adder_1_out), .b(shifter_1_out), .out(adder_2_out));  // open: cin, cout
  Multiplexer #(.width(32)) multiplexer_1 (
    .in0(adder_1_out), .in1(adder_2_out), .out(multiplexer_1_out), .sel(Branch));  // open: en
endmodule

module Controller (
  input  [5:0] opcode,
  input  [5:0] func,
  output RegRead_2,
  output RegWrite,
  output extop,
  output MemWrite,
  output RegRead_1,
  output Alu_2,
  output MemRead,
  output Branch,
  output [2:0] Alu_control,
  output RegDst,
  output sw
);

  wire addu, beq, comparator_1_eq, lw, not_1_out, not_2_out, not_3_out, not_4_out, not_5_out, not_6_out,
       not_7_out, not_8_out, not_9_out, not_10_out, not_11_out, not_12_out, ori, subu;

  Comparator #(.width(6), .mode("unsigned")) comparator_1 (
    .a(opcode), .b({6{1'b0}}), .eq(comparator_1_eq));  // open: gt, lt
  not not_1 (not_1_out, opcode[5]);
  not not_2 (not_2_out, opcode[3]);
  not not_3 (not_3_out, opcode[4]);
  not not_4 (not_4_out, opcode[1]);
  not not_5 (not_5_out, opcode[2]);
  not not_6 (not_6_out, opcode[0]);
  not not_7 (not_7_out, func[5]);
  not not_8 (not_8_out, func[4]);
  not not_9 (not_9_out, func[3]);
  not not_10 (not_10_out, func[2]);
  not not_11 (not_11_out, func[0]);
  not not_12 (not_12_out, func[1]);
  and u_addu (addu, comparator_1_eq, func[5], not_8_out, not_9_out, not_10_out, not_12_out, func[0]);
  and u_subu (subu, comparator_1_eq, func[5], not_8_out, not_9_out, not_10_out, func[1], func[0]);
  and u_ori (ori, not_1_out, not_3_out, opcode[3], opcode[2], not_4_out, opcode[0]);
  and u_lw (lw, opcode[5], not_3_out, not_2_out, not_5_out, opcode[1], opcode[0]);
  and u_sw (sw, opcode[5], not_3_out, opcode[3], not_5_out, opcode[1], opcode[0]);
  and u_beq (beq, not_1_out, not_3_out, not_2_out, opcode[2], not_4_out, not_6_out);
  and lui (RegRead_1, not_1_out, not_3_out, opcode[3], opcode[2], opcode[1], opcode[0]);
  or or_1 (RegRead_2, addu, subu, beq, sw);
  or or_2 (RegWrite, addu, subu, ori, lw, RegRead_1);
  or or_3 (extop, lw, sw, beq);
  buf or_4 (MemWrite, sw);  // OR_Gate
  or or_5 (Alu_2, ori, lw, sw, RegRead_1);
  buf or_6 (MemRead, lw);  // OR_Gate
  buf or_7 (Branch, beq);  // OR_Gate
  or or_8 (Alu_control[0], ori, subu, beq);
  or or_9 (Alu_control[1], lw, sw, RegRead_1, addu, subu, beq);
  buf or_10 (Alu_control[2], 1'b0);  // OR_Gate
  or or_11 (RegDst, addu, subu);

  // Other names for the same wires on the sheet: lui = RegRead_1

  // Notes on the sheet:
  //   000:&,001:|,010:+,011:-,100:equal
endmodule

module DM (
  input  [4:0] A,
  input  [31:0] WD,
  input  WE,
  input  reset,
  input  clk,
  input  MemRead,
  output [31:0] RD
);

  RAM #(.addrWidth(5), .dataWidth(32), .bus("separate")) ram_1 (
    .addr(A), .din(WD), .data(RD), .str(WE), .clk(clk), .ld(MemRead), .clr(reset));  // open: sel
endmodule

module ALU (
  input  [31:0] A1,
  input  [31:0] A2,
  input  [2:0] ALU_control,
  output [31:0] out,
  output zero
);

  wire [31:0] adder_1_out, and_1_out, or_1_out, subtractor_1_out;

  // Probe on subtractor_1_out
  assign and_1_out = A1 & A2;  // AND_Gate and_1, 32 bits wide
  assign or_1_out = A1 | A2;  // OR_Gate or_1, 32 bits wide
  Adder #(.width(32)) adder_1 (.a(A1), .b(A2), .out(adder_1_out));  // open: cin, cout
  Subtractor #(.width(32)) subtractor_1 (.a(A1), .b(A2), .out(subtractor_1_out));  // open: bin, bout
  Multiplexer #(.select(3), .width(32)) multiplexer_1 (
    .in0(and_1_out), .in1(or_1_out), .in2(adder_1_out), .in3(subtractor_1_out), .out(out), .sel(ALU_control));  // open: in4, in5, in6, in7, en
  Comparator #(.width(32), .mode("unsigned")) comparator_1 (.a(out), .b({32{1'b0}}), .eq(zero));  // open: gt, lt

  // Other names for the same wires on the sheet: alu_con[2:0] = ALU_control

  // Notes on the sheet:
  //   000:&,001:|,010:+,011:-
endmodule

// Ext
module ext (
  input  [15:0] imm_16,
  input  extop,
  output [31:0] result
);

  wire [31:0] bit_extender_1_out, bit_extender_2_out;

  assign bit_extender_1_out = {{16{imm_16[15]}}, imm_16};  // Bit_Extender bit_extender_1
  assign bit_extender_2_out = {{16{1'b0}}, imm_16};  // Bit_Extender bit_extender_2
  Multiplexer #(.width(32)) multiplexer_1 (
    .in0(bit_extender_2_out), .in1(bit_extender_1_out), .out(result), .sel(extop));  // open: en
endmodule
