// Logisim project mod5.circ as structural Verilog: 3 circuits, main circuit mod5
module mod5 (
  input  in_1,
  output out_2,
  output out_3,
  output out_4,
  output out_5,
  output out_6
);

  wire clock_1_out;
  wire [1:0] register_1_q, \状态转移_1_c_0 ;

  \状态转移  \u_状态转移_1  (
    .c0(register_1_q[0]), .c1(register_1_q[1]), .in(in_1), .c_0(\状态转移_1_c_0 [0]), .c_1(\状态转移_1_c_0 [1]));
  Register #(.width(2)) register_1 (.D(\状态转移_1_c_0 ), .Q(register_1_q), .clk(clock_1_out));  // open: en, clr
  Clock clock_1 (.out(clock_1_out));
  \状态输出  \u_状态输出_1  (
    .c0(register_1_q[0]), .c1(register_1_q[1]), .in(in_1), .s0(out_2), .s1(out_3), .s2(out_4), .s3(out_5),
    .s4(out_6));
endmodule

module \状态转移  (
  input  c0,
  input  c1,
  input  in,
  output c_0,
  output c_1
);

  wire and_1_out, and_2_out, and_3_out, and_4_out, and_5_out, and_6_out, not_1_out, not_2_out, not_3_out,
       not_4_out, not_5_out, not_6_out, not_7_out, not_8_out;

  not not_1 (not_1_out, c0);
  not not_2 (not_2_out, c1);
  not not_3 (not_3_out, c0);
  not not_4 (not_4_out, c1);
  not not_5 (not_5_out, c0);
  not not_6 (not_6_out, in);
  not not_7 (not_7_out, c1);
  not not_8 (not_8_out, in);
  and and_1 (and_1_out, not_1_out, c1);
  and and_2 (and_2_out, c0, not_2_out);
  and and_3 (and_3_out, not_3_out, not_4_out, in);
  and and_4 (and_4_out, not_5_out, c1, not_6_out);
  and and_5 (and_5_out, c0, not_7_out, not_8_out);
  and and_6 (and_6_out, c0, c1, in);
  or or_1 (c_0, and_1_out, and_2_out);
  or or_2 (c_1, and_3_out, and_4_out, and_5_out, and_6_out);
endmodule

module \状态输出  (
  input  c0,
  input  c1,
  input  in,
  output s0,
  output s1,
  output s2,
  output s3,
  output s4
);

  wire and_1_out, and_2_out, and_3_out, and_4_out, and_5_out, and_6_out, and_7_out, and_8_out, not_1_out,
       not_2_out, not_3_out, not_4_out, not_5_out, not_6_out, not_7_out, not_8_out, not_9_out, not_10_out,
       not_11_out, not_12_out;

  not not_1 (not_1_out, c0);
  not not_2 (not_2_out, c1);
  not not_3 (not_3_out, in);
  not not_4 (not_4_out, in);
  not not_5 (not_5_out, c0);
  not not_6 (not_6_out, c1);
  not not_7 (not_7_out, c0);
  not not_8 (not_8_out, c1);
  not not_9 (not_9_out, c0);
  not not_10 (not_10_out, in);
  not not_11 (not_11_out, c1);
  not not_12 (not_12_out, in);
  and and_1 (and_1_out, not_1_out, not_2_out, not_3_out);
  and and_2 (and_2_out, c0, c1, not_4_out);
  and and_3 (and_3_out, not_5_out, not_6_out, in);
  and and_4 (and_4_out, c0, c1, in);
  and and_5 (and_5_out, not_7_out, c1, in);
  and and_6 (and_6_out, c0, not_8_out, in);
  and and_7 (and_7_out, not_9_out, c1, not_10_out);
  and and_8 (and_8_out, c0, not_11_out, not_12_out);
  or or_1 (s1, and_1_out, and_2_out);
  or or_2 (s2, and_3_out, and_4_out);
  or or_3 (s3, and_5_out, and_6_out);
  or or_4 (s4, and_7_out, and_8_out);

  assign s0 = 1'b0;
endmodule
