// Logisim project practice.circ as structural Verilog: 1 circuit, main circuit main
module main (
);

  Clock clock_1 ();  // open: out
  Register #(.width(16)) register_1 ();  // open: D, en, Q, clk, clr
  ROM #(.dataWidth(32)) rom_1 ();  // open: addr, data, sel
  RAM #(.dataWidth(32), .bus("separate")) ram_1 ();  // open: addr, din, data, str, sel, clk, ld, clr

  // Notes on the sheet:
  //   contents of rom_1 (hex, n*v repeats v):
  //   0 12
endmodule
