// Logisim project 交通灯控制器.circ as structural Verilog: 1 circuit, main circuit main
module main (
  input  in_1,
  input  in_2,
  input  RESET,
  output out_4,
  output out_5,
  output out_6,
  output out_7
);

  wire and_1_out, and_2_out, clock_1_out, d_ff_2_q, not_1_out, not_2_out, not_3_out, not_4_out, not_5_out,
       not_6_out, or_1_out, xor_1_out;

  not not_1 (not_1_out, d_ff_2_q);
  not not_2 (not_2_out, out_4);
  not not_3 (not_3_out, in_1);
  not not_4 (not_4_out, d_ff_2_q);
  not not_5 (not_5_out, in_2);
  and and_1 (and_1_out, not_1_out, not_2_out, not_3_out);
  and and_2 (and_2_out, out_4, not_4_out, not_5_out);
  xor xor_1 (xor_1_out, out_4, d_ff_2_q);
  or or_1 (or_1_out, and_1_out, and_2_out);
  Clock clock_1 (.out(clock_1_out));
  D_Flip_Flop d_ff_1 (.clk(clock_1_out), .D(xor_1_out), .Q(out_4), .reset(RESET));  // open: Qn, preset, en
  D_Flip_Flop d_ff_2 (.clk(clock_1_out), .D(or_1_out), .Q(d_ff_2_q), .reset(RESET));  // open: Qn, preset, en
  not not_6 (not_6_out, out_4);
  not not_7 (out_6, out_4);
  and and_3 (out_5, not_6_out, d_ff_2_q);
  and and_4 (out_7, out_4, d_ff_2_q);
endmodule
