// Logisim project 右移.circ as structural Verilog: 1 circuit, main circuit main
module main (
  input  [7:0] in_1,
  input  in_2,
  output [7:0] out_3
);

  wire clock_1_out, comparator_1_gt;
  wire [7:0] multiplexer_1_out, register_1_q;

  Multiplexer #(.width(8)) multiplexer_1 (
    .in0(in_1), .in1(register_1_q), .out(multiplexer_1_out), .sel(comparator_1_gt));  // open: en
  Shifter #(.shift("lr")) shifter_1 (.in(multiplexer_1_out), .\dist (3'b001), .out(out_3));
  Clock clock_1 (.out(clock_1_out));
  Register register_1 (.D(out_3), .Q(register_1_q), .clk(clock_1_out), .clr(in_2));  // open: en
  Comparator comparator_1 (.a(register_1_q), .b({8{1'b0}}), .gt(comparator_1_gt));  // open: eq, lt
endmodule
