// Logisim project 斐波那契.circ as structural Verilog: 3 circuits, main circuit main
module main (
  input  [31:0] in_1,
  output [31:0] out_2
);

  wire clock_1_out, comparator_1_eq, comparator_1_gt, comparator_1_lt, \initial , not_1_out, or_1_out;
  wire [31:0] and_1_out, and_2_out, bit_extender_1_out, counter_1_q, multiplexer_1_out, register_1_q,
       register_2_q, \转移_1_out_3 , \转移_1_out_4 ;

  Counter #(.width(32), .ongoal("stay")) counter_1 (
    .Q(counter_1_q), .clk(clock_1_out));  // open: load, D, count, carry, clr
  assign bit_extender_1_out = {{31{1'b1}}, comparator_1_gt};  // Bit_Extender bit_extender_1
  Comparator #(.width(32), .mode("unsigned")) comparator_1 (
    .a(in_1), .b(counter_1_q), .gt(comparator_1_gt), .eq(comparator_1_eq), .lt(comparator_1_lt));
  or or_1 (or_1_out, comparator_1_lt, comparator_1_eq);
  assign and_1_out = bit_extender_1_out & \转移_1_out_3 ;  // AND_Gate and_1, 32 bits wide
  Multiplexer #(.width(32)) multiplexer_1 (
    .in0(32'h1), .in1(and_2_out), .out(multiplexer_1_out), .sel(\initial ));  // open: en
  assign and_2_out = bit_extender_1_out & \转移_1_out_4 ;  // AND_Gate and_2, 32 bits wide
  not not_1 (not_1_out, or_1_out);
  Clock clock_1 (.out(clock_1_out));
  Register #(.width(32)) register_1 (.D(and_1_out), .en(not_1_out), .Q(register_1_q), .clk(clock_1_out));  // open: clr
  Register #(.width(32)) register_2 (
    .D(multiplexer_1_out), .en(not_1_out), .Q(register_2_q), .clk(clock_1_out));  // open: clr
  Multiplexer #(.width(32)) multiplexer_2 (
    .in0({32{1'b0}}), .in1(\转移_1_out_3 ), .out(out_2), .sel(or_1_out));  // open: en
  \转移  \u_转移_1  (.in_1(register_1_q), .in_2(register_2_q), .out_3(\转移_1_out_3 ), .out_4(\转移_1_out_4 ));
  Counter #(.width(1), .max('h1), .ongoal("stay")) counter_2 (
    .Q(\initial ), .clk(clock_1_out));  // open: load, D, count, carry, clr
endmodule

module \转移  (
  input  [31:0] in_1,
  input  [31:0] in_2,
  output [31:0] out_3,
  output [31:0] out_4
);

  Adder #(.width(32)) adder_1 (.a(in_1), .b(in_2), .out(out_4));  // open: cin, cout

  assign out_3 = in_2;
endmodule

module _1 (
  output [3:0] out_1
);

  wire clock_1_out, undriven;

  Counter #(.width(4), .max('hf)) counter_1 (
    .D(4'b0000), .Q(out_1), .clk(clock_1_out), .clr(undriven));  // open: load, count, carry
  Clock clock_1 (.out(clock_1_out));
endmodule
