// Logisim project 斐波那契困难版.circ as structural Verilog: 3 circuits, main circuit 矩阵乘法
module \矩阵乘法  (
  input  [31:0] i0,
  input  [31:0] i1,
  input  [31:0] i2,
  input  [31:0] i3,
  output [31:0] out_0,
  output [31:0] out_1,
  output [31:0] out_2,
  output [31:0] out_3
);

  wire [31:0] multiplier_1_out, multiplier_2_out, multiplier_3_out, multiplier_4_out, multiplier_5_out,
       multiplier_6_out, multiplier_7_out, multiplier_8_out;

  Multiplier #(.width(32)) multiplier_1 (.a(i0), .b(i0), .out(multiplier_1_out));  // open: cin, cout
  Multiplier #(.width(32)) multiplier_2 (.a(i2), .b(i1), .out(multiplier_2_out));  // open: cin, cout
  Multiplier #(.width(32)) multiplier_3 (.a(i0), .b(i2), .out(multiplier_3_out));  // open: cin, cout
  Multiplier #(.width(32)) multiplier_4 (.a(i2), .b(i3), .out(multiplier_4_out));  // open: cin, cout
  Multiplier #(.width(32)) multiplier_5 (.a(i0), .b(i2), .out(multiplier_5_out));  // open: cin, cout
  Multiplier #(.width(32)) multiplier_6 (.a(i2), .b(i3), .out(multiplier_6_out));  // open: cin, cout
  Multiplier #(.width(32)) multiplier_7 (.a(i2), .b(i2), .out(multiplier_7_out));  // open: cin, cout
  Multiplier #(.width(32)) multiplier_8 (.a(i3), .b(i3), .out(multiplier_8_out));  // open: cin, cout
  Adder #(.width(32)) adder_1 (.a(multiplier_1_out), .b(multiplier_2_out), .out(out_0));  // open: cin, cout
  Adder #(.width(32)) adder_2 (.a(multiplier_3_out), .b(multiplier_4_out), .out(out_1));  // open: cin, cout
  Adder #(.width(32)) adder_3 (.a(multiplier_5_out), .b(multiplier_6_out), .out(out_2));  // open: cin, cout
  Adder #(.width(32)) adder_4 (.a(multiplier_7_out), .b(multiplier_8_out), .out(out_3));  // open: cin, cout
endmodule

module main (
  input  [31:0] in,
  input  in_2,
  output [31:0] out_3
);

  wire and_2_out, clk, comparator_3_eq, comparator_4_gt, comparator_5_gt, comparator_6_gt, comparator_7_gt,
       freeze, judge, not_1_out, not_2_out, not_3_out, one;
  wire [5:0] counter;
  wire [31:0] a00, a01, a10, a11, and_1_out, b00, b01, b10, b11, c00, c01, c10, c11, multiplexer_1_out,
       multiplexer_2_out, multiplexer_4_out, multiplexer_5_out, multiplexer_6_out, multiplexer_8_out,
       multiplexer_9_out, multiplexer_10_out, multiplexer_13_out, multiplexer_16_out, multiplexer_17_out,
       now_value, register_3_q, shifter_1_out, subtractor_1_out, \矩阵乘法1_1_out_9 , \矩阵乘法1_1_out_10 ,
       \矩阵乘法1_1_out_11 , \矩阵乘法1_1_out_12 , \矩阵乘法_1_out_0 , \矩阵乘法_1_out_1 , \矩阵乘法_1_out_2 , \矩阵乘法_1_out_3 ;

  Clock clock_1 (.out(clk));
  Counter #(.width(1), .max('h1), .ongoal("stay")) counter_1 (
    .Q(one), .clk(clk), .clr(in_2));  // open: load, D, count, carry
  Counter #(.width(6), .max('h3f), .ongoal("stay")) counter_2 (
    .Q(counter), .clk(clk), .clr(in_2));  // open: load, D, count, carry
  Multiplexer #(.width(32)) multiplexer_1 (
    .in0(32'h1), .in1(\矩阵乘法_1_out_0 ), .out(multiplexer_1_out), .sel(one));  // open: en
  Multiplexer #(.width(32)) multiplexer_2 (
    .in0(32'h1), .in1(\矩阵乘法_1_out_2 ), .out(multiplexer_2_out), .sel(one));  // open: en
  Comparator #(.width(32), .mode("unsigned")) comparator_1 (
    .a(now_value), .b({32{1'b0}}), .eq(freeze));  // open: gt, lt
  // Probe on now_value
  assign and_1_out = now_value & 32'h1;  // AND_Gate and_1, 32 bits wide
  Subtractor #(.width(32)) subtractor_1 (.a(in), .b(32'h1), .out(subtractor_1_out));  // open: bin, bout
  \矩阵乘法  \u_矩阵乘法_1  (
    .i0(a00), .i1(a01), .i2(a10), .i3(a11), .out_0(\矩阵乘法_1_out_0 ), .out_1(\矩阵乘法_1_out_1 ),
    .out_2(\矩阵乘法_1_out_2 ), .out_3(\矩阵乘法_1_out_3 ));
  Comparator #(.width(32), .mode("unsigned")) comparator_2 (.a(and_1_out), .b({32{1'b0}}), .gt(judge));  // open: eq, lt
  Shifter #(.width(32), .shift("lr")) shifter_1 (.in(register_3_q), .\dist (5'b00001), .out(shifter_1_out));
  Clock clock_2 ();  // open: out
  Register #(.width(32)) register_1 (.D(multiplexer_1_out), .Q(a00), .clk(clk), .clr(in_2));  // open: en
  Register #(.width(32)) register_2 (.D(multiplexer_2_out), .Q(a10), .clk(clk), .clr(in_2));  // open: en
  Multiplexer #(.width(32)) multiplexer_3 (
    .in0(shifter_1_out), .in1(subtractor_1_out), .out(now_value), .sel(comparator_3_eq));  // open: en
  not not_1 (not_1_out, freeze);
  and and_2 (and_2_out, one, not_1_out);
  Register #(.width(32)) register_3 (.D(now_value), .en(and_2_out), .Q(register_3_q), .clk(clk), .clr(in_2));
  Multiplexer #(.width(32)) multiplexer_4 (
    .in0(32'h1), .in1(\矩阵乘法_1_out_1 ), .out(multiplexer_4_out), .sel(one));  // open: en
  Multiplexer #(.width(32)) multiplexer_5 (
    .in0({32{1'b0}}), .in1(\矩阵乘法_1_out_3 ), .out(multiplexer_5_out), .sel(one));  // open: en
  Comparator #(.width(32), .mode("unsigned")) comparator_3 (
    .a(register_3_q), .b({32{1'b0}}), .eq(comparator_3_eq));  // open: gt, lt
  Register #(.width(32)) register_4 (.D(multiplexer_4_out), .Q(a01), .clk(clk), .clr(in_2));  // open: en
  Register #(.width(32)) register_5 (.D(multiplexer_5_out), .Q(a11), .clk(clk), .clr(in_2));  // open: en
  Multiplexer #(.width(32)) multiplexer_6 (
    .in0({32{1'b0}}), .in1(32'h1), .out(multiplexer_6_out), .sel(judge));  // open: en
  Multiplexer #(.width(32)) multiplexer_7 (.in0({32{1'b0}}), .in1(b00), .out(out_3), .sel(freeze));  // open: en
  Multiplexer #(.width(32)) multiplexer_8 (
    .in0(32'h1), .in1(c00), .out(multiplexer_8_out), .sel(comparator_4_gt));  // open: en
  Comparator #(.width(6), .mode("unsigned")) comparator_4 (
    .a(counter), .b(6'b000001), .gt(comparator_4_gt));  // open: eq, lt
  Multiplexer #(.width(32)) multiplexer_9 (
    .in0(multiplexer_6_out), .in1(c10), .out(multiplexer_9_out), .sel(comparator_5_gt));  // open: en
  Comparator #(.width(6), .mode("unsigned")) comparator_5 (
    .a(counter), .b(6'b000001), .gt(comparator_5_gt));  // open: eq, lt
  \矩阵乘法1  \u_矩阵乘法1_1  (
    .A_0_0(a00), .A_0_1(a01), .A_1_0(a10), .A_1_1(a11), .B_0_0(b00), .B_0_1(b01), .B_1_0(b10), .B_1_1(b11),
    .out_9(\矩阵乘法1_1_out_9 ), .out_10(\矩阵乘法1_1_out_10 ), .out_11(\矩阵乘法1_1_out_11 ), .out_12(\矩阵乘法1_1_out_12 ));
  Register #(.width(32)) out_0 (.D(multiplexer_8_out), .en(not_2_out), .Q(b00), .clk(clk), .clr(in_2));
  Register #(.width(32)) out_2 (.D(multiplexer_9_out), .en(not_2_out), .Q(b10), .clk(clk), .clr(in_2));
  not not_2 (not_2_out, freeze);
  Multiplexer #(.width(32)) multiplexer_10 (
    .in0({32{1'b0}}), .in1(32'h1), .out(multiplexer_10_out), .sel(judge));  // open: en
  Multiplexer #(.width(32)) multiplexer_11 (.in0(b00), .in1(\矩阵乘法1_1_out_9 ), .out(c00), .sel(judge));  // open: en
  Multiplexer #(.width(32)) multiplexer_12 (.in0(b01), .in1(\矩阵乘法1_1_out_10 ), .out(c01), .sel(judge));  // open: en
  Multiplexer #(.width(32)) multiplexer_13 (
    .in0(32'h1), .in1({32{1'b0}}), .out(multiplexer_13_out), .sel(judge));  // open: en
  // Probe on nothing
  Multiplexer #(.width(32)) multiplexer_14 (.in0(b10), .in1(\矩阵乘法1_1_out_11 ), .out(c10), .sel(judge));  // open: en
  Multiplexer #(.width(32)) multiplexer_15 (.in0(b11), .in1(\矩阵乘法1_1_out_12 ), .out(c11), .sel(judge));  // open: en
  Multiplexer #(.width(32)) multiplexer_16 (
    .in0(multiplexer_10_out), .in1(c01), .out(multiplexer_16_out), .sel(comparator_6_gt));  // open: en
  Comparator #(.width(6), .mode("unsigned")) comparator_6 (
    .a(counter), .b(6'b000001), .gt(comparator_6_gt));  // open: eq, lt
  Multiplexer #(.width(32)) multiplexer_17 (
    .in0(multiplexer_13_out), .in1(c11), .out(multiplexer_17_out), .sel(comparator_7_gt));  // open: en
  Register #(.width(32)) out_1 (.D(multiplexer_16_out), .en(not_3_out), .Q(b01), .clk(clk), .clr(in_2));
  Comparator #(.width(6), .mode("unsigned")) comparator_7 (
    .a(counter), .b(6'b000001), .gt(comparator_7_gt));  // open: eq, lt
  not not_3 (not_3_out, freeze);
  Register #(.width(32)) u_out_3 (.D(multiplexer_17_out), .en(not_3_out), .Q(b11), .clk(clk), .clr(in_2));

  // Other names for the same wires on the sheet: re = in_2
endmodule

module \矩阵乘法1  (
  input  [31:0] A_0_0,
  input  [31:0] A_0_1,
  input  [31:0] A_1_0,
  input  [31:0] A_1_1,
  input  [31:0] B_0_0,
  input  [31:0] B_0_1,
  input  [31:0] B_1_0,
  input  [31:0] B_1_1,
  output [31:0] out_9,
  output [31:0] out_10,
  output [31:0] out_11,
  output [31:0] out_12
);

  wire [31:0] multiplier_1_out, multiplier_2_out, multiplier_3_out, multiplier_4_out, multiplier_5_out,
       multiplier_6_out, multiplier_7_out, multiplier_8_out;

  Multiplier #(.width(32)) multiplier_1 (.a(A_0_0), .b(B_0_0), .out(multiplier_1_out));  // open: cin, cout
  Multiplier #(.width(32)) multiplier_2 (.a(A_0_1), .b(B_1_0), .out(multiplier_2_out));  // open: cin, cout
  Multiplier #(.width(32)) multiplier_3 (.a(A_0_0), .b(B_0_1), .out(multiplier_3_out));  // open: cin, cout
  Multiplier #(.width(32)) multiplier_4 (.a(A_0_1), .b(B_1_1), .out(multiplier_4_out));  // open: cin, cout
  Multiplier #(.width(32)) multiplier_5 (.a(A_1_0), .b(B_0_0), .out(multiplier_5_out));  // open: cin, cout
  Multiplier #(.width(32)) multiplier_6 (.a(A_1_1), .b(B_1_0), .out(multiplier_6_out));  // open: cin, cout
  Multiplier #(.width(32)) multiplier_7 (.a(A_1_0), .b(B_0_1), .out(multiplier_7_out));  // open: cin, cout
  Multiplier #(.width(32)) multiplier_8 (.a(A_1_1), .b(B_1_1), .out(multiplier_8_out));  // open: cin, cout
  Adder #(.width(32)) adder_1 (.a(multiplier_1_out), .b(multiplier_2_out), .out(out_9));  // open: cin, cout
  Adder #(.width(32)) adder_2 (.a(multiplier_3_out), .b(multiplier_4_out), .out(out_10));  // open: cin, cout
  Adder #(.width(32)) adder_3 (.a(multiplier_5_out), .b(multiplier_6_out), .out(out_11));  // open: cin, cout
  Adder #(.width(32)) adder_4 (.a(multiplier_7_out), .b(multiplier_8_out), .out(out_12));  // open: cin, cout
endmodule
