// Logisim project 锁存器.circ as structural Verilog: 4 circuits, main circuit SR
module SR (
  input  R,
  input  R_2,
  input  S,
  input  S_2,
  output Q,
  output nQ,
  output nQ_2,
  output Q_2
);

  wire and_1_out, and_2_out, not_3_out, not_4_out, or_1_out, or_2_out;

  or or_1 (or_1_out, R, nQ_2);
  or or_2 (or_2_out, Q, S);
  not not_1 (Q, or_1_out);
  not not_2 (nQ_2, or_2_out);
  not not_3 (not_3_out, R_2);
  not not_4 (not_4_out, S_2);
  and and_1 (and_1_out, not_3_out, Q_2);
  and and_2 (and_2_out, nQ, not_4_out);
  not not_5 (nQ, and_1_out);
  not not_6 (Q_2, and_2_out);
endmodule

module SR2 (
  input  R,
  input  S,
  output Q,
  output nQ
);

  nor nor_1 (Q, R, nQ);
  nor nor_2 (nQ, Q, S);
endmodule

module \D锁存器  (
  input  CLK,
  input  D,
  output Q,
  output nQ
);

  wire and_1_out, and_2_out, not_1_out;

  not not_1 (not_1_out, D);
  and and_1 (and_1_out, CLK, not_1_out);
  and and_2 (and_2_out, CLK, D);
  SR2 sr2_1 (.R(and_1_out), .S(and_2_out), .Q(Q), .nQ(nQ));
endmodule

module \D触发器  (
  input  D,
  output Q,
  output nQ
);

  wire CLK_out, not_1_out, \主_q ;

  not not_1 (not_1_out, CLK_out);
  \D锁存器  \u_主  (.CLK(not_1_out), .D(D), .Q(\主_q ));  // open: nQ
  Clock CLK (.out(CLK_out));
  \D锁存器  \u_从  (.CLK(CLK_out), .D(\主_q ), .Q(Q), .nQ(nQ));
endmodule
