// Logisim project practice.circ as structural Verilog: 7 circuits, main circuit main
module main (
  input  in_00,
  input  [7:0] in_2,
  input  in_01,
  input  in_4,
  input  in_5,
  input  in_10,
  input  in_7,
  input  in_11,
  input  in_9,
  input  select_1,
  input  select_0,
  output [1:0] out_12,
  output out_13,
  output out_14
);

  wire multiplexer_2_out, multiplexer_3_out;

  Multiplexer multiplexer_1 (.in0(in_5), .in1(in_7), .out(out_14), .sel(in_4), .en(in_9));
  and and_1 (out_12[0], in_2[0], in_2[2]);
  xnor xnor_1 (out_12[1], in_2[4], in_2[6]);
  Multiplexer multiplexer_2 (.in0(in_00), .in1(in_01), .out(multiplexer_2_out), .sel(select_0));  // open: en
  Multiplexer multiplexer_3 (.in0(in_10), .in1(in_11), .out(multiplexer_3_out), .sel(select_0));  // open: en
  Multiplexer multiplexer_4 (
    .in0(multiplexer_2_out), .in1(multiplexer_3_out), .out(out_13), .sel(select_1));  // open: en
endmodule

module _2_1_mux (
  input  in_0,
  input  in_1,
  input  select,
  output out_4
);

  wire and_1_out, and_2_out, not_1_out;

  not not_1 (not_1_out, select);
  and and_1 (and_1_out, in_1, select);
  and and_2 (and_2_out, in_0, not_1_out);
  or or_1 (out_4, and_2_out, and_1_out);
endmodule

module _4_1_mux (
  input  in_00,
  input  in_01,
  input  in_10,
  input  in_11,
  input  select_0,
  input  select_1,
  output out
);

  wire n2_1_mux_1_out_4, n2_1_mux_2_out_4;

  _2_1_mux u_2_1_mux_1 (.in_0(in_00), .in_1(in_01), .select(select_1), .out_4(n2_1_mux_1_out_4));
  _2_1_mux u_2_1_mux_2 (.in_0(in_10), .in_1(in_11), .select(select_1), .out_4(n2_1_mux_2_out_4));
  _2_1_mux u_2_1_mux_3 (.in_0(n2_1_mux_1_out_4), .in_1(n2_1_mux_2_out_4), .select(select_0), .out_4(out));
endmodule

module _1_2_de_mux (
  input  in_1,
  input  in_2,
  output out_3,
  output out_4
);

  wire not_1_out;

  not not_1 (not_1_out, in_2);
  and and_1 (out_3, in_1, not_1_out);
  and and_2 (out_4, in_1, in_2);
endmodule

module _1_4_de_mux (
  input  in_1,
  input  in_2,
  input  in_3,
  output out_4,
  output out_5,
  output out_6,
  output out_7
);

  wire n1_2_de_mux_1_out_3, n1_2_de_mux_1_out_4;

  _1_2_de_mux u_1_2_de_mux_1 (.in_1(in_1), .in_2(in_2), .out_3(n1_2_de_mux_1_out_3), .out_4(n1_2_de_mux_1_out_4));
  _1_2_de_mux u_1_2_de_mux_2 (.in_1(n1_2_de_mux_1_out_3), .in_2(in_3), .out_3(out_4), .out_4(out_5));
  _1_2_de_mux u_1_2_de_mux_3 (.in_1(n1_2_de_mux_1_out_4), .in_2(in_3), .out_3(out_6), .out_4(out_7));
endmodule

module decode (
  input  in_1,
  input  [1:0] in_2,
  output out_3,
  output out_4
);

  wire decoder_2_out0, decoder_2_out1, decoder_2_out2, decoder_2_out3;

  Decoder decoder_1 (.out0(out_3), .out1(out_4), .sel(in_1));  // open: en
  Decoder #(.select(2)) decoder_2 (
    .out0(decoder_2_out0), .out1(decoder_2_out1), .out2(decoder_2_out2), .out3(decoder_2_out3), .sel(in_2),
    .en(1'b1));
  LED _0 (.in(decoder_2_out0));
  LED _1 (.in(decoder_2_out1));
  LED _2 (.in(decoder_2_out2));
  LED _3 (.in(decoder_2_out3));
endmodule

module prac (
  input  in_1,
  input  in_2
);

  _1_4_de_mux u_1_4_de_mux_1 (.in_2(in_1), .in_3(in_2));  // open: in_1, out_4, out_5, out_6, out_7
endmodule
