// Logisim project swap.circ as structural Verilog
module _1bit_swap (
  input  a,
  input  b,
  input  c,
  output o1,
  output o2
);

  wire and_1_out, and_2_out, and_3_out, and_4_out, not_1_out, not_2_out;

  not not_1 (not_1_out, c);
  not not_2 (not_2_out, c);
  and and_1 (and_1_out, b, c);
  and and_2 (and_2_out, a, not_1_out);
  and and_3 (and_3_out, b, not_2_out);
  and and_4 (and_4_out, a, c);
  or or_1 (o1, and_1_out, and_2_out);
  or or_2 (o2, and_3_out, and_4_out);
endmodule

module _4bit_swap (
  input  [3:0] in_1,
  input  [3:0] in_2,
  input  in_3,
  output [3:0] out_1,
  output [3:0] out_2
);

  _1bit_swap _0 (.a(in_1[0]), .b(in_2[0]), .c(in_3), .o1(out_1[0]), .o2(out_2[0]));
  _1bit_swap _1 (.a(in_1[1]), .b(in_2[1]), .c(in_3), .o1(out_1[1]), .o2(out_2[1]));
  _1bit_swap _2 (.a(in_1[2]), .b(in_2[2]), .c(in_3), .o1(out_1[2]), .o2(out_2[2]));
  _1bit_swap _3 (.a(in_1[3]), .b(in_2[3]), .c(in_3), .o1(out_1[3]), .o2(out_2[3]));

  // Other names for the same wires on the sheet: _00 = in_1[0]; _01 = in_1[1]; _02 = in_1[2]; _03 = in_1[3];
  //   _10 = in_2[0]; _11 = in_2[1]; _12 = in_2[2]; _13 = in_2[3]
endmodule

module _4bit_sort (
  input  [3:0] A,
  input  [3:0] B,
  input  [3:0] C,
  input  [3:0] D,
  output [3:0] out_5,
  output [3:0] out_6,
  output [3:0] out_7,
  output [3:0] out_8
);

  wire comparator_1_gt, comparator_2_gt, comparator_3_gt, comparator_4_gt, comparator_5_gt;
  wire [3:0] n4bit_swap_1_out_1, n4bit_swap_1_out_2, n4bit_swap_2_out_1, n4bit_swap_2_out_2,
       n4bit_swap_3_out_2, n4bit_swap_4_out_1;

  Comparator #(.width(4), .mode("unsigned")) comparator_1 (.a(A), .b(B), .gt(comparator_1_gt));  // open: eq, lt
  Comparator #(.width(4), .mode("unsigned")) comparator_2 (.a(C), .b(D), .gt(comparator_2_gt));  // open: eq, lt
  _4bit_swap u_4bit_swap_1 (
    .in_1(A), .in_2(B), .in_3(comparator_1_gt), .out_1(n4bit_swap_1_out_1), .out_2(n4bit_swap_1_out_2));
  _4bit_swap u_4bit_swap_2 (
    .in_1(C), .in_2(D), .in_3(comparator_2_gt), .out_1(n4bit_swap_2_out_1), .out_2(n4bit_swap_2_out_2));
  Comparator #(.width(4), .mode("unsigned")) comparator_3 (
    .a(n4bit_swap_1_out_1), .b(n4bit_swap_2_out_1), .gt(comparator_3_gt));  // open: eq, lt
  _4bit_swap u_4bit_swap_3 (
    .in_1(n4bit_swap_1_out_1), .in_2(n4bit_swap_2_out_1), .in_3(comparator_3_gt), .out_1(out_5),
    .out_2(n4bit_swap_3_out_2));
  Comparator #(.width(4), .mode("unsigned")) comparator_4 (
    .a(n4bit_swap_1_out_2), .b(n4bit_swap_2_out_2), .gt(comparator_4_gt));  // open: eq, lt
  _4bit_swap u_4bit_swap_4 (
    .in_1(n4bit_swap_1_out_2), .in_2(n4bit_swap_2_out_2), .in_3(comparator_4_gt), .out_1(n4bit_swap_4_out_1),
    .out_2(out_8));
  Comparator #(.width(4), .mode("unsigned")) comparator_5 (
    .a(n4bit_swap_3_out_2), .b(n4bit_swap_4_out_1), .gt(comparator_5_gt));  // open: eq, lt
  _4bit_swap u_4bit_swap_5 (
    .in_1(n4bit_swap_3_out_2), .in_2(n4bit_swap_4_out_1), .in_3(comparator_5_gt), .out_1(out_6), .out_2(out_7));
endmodule
