// Logisim project work.circ as structural Verilog
module work1 (
  input  s0,
  input  s1,
  input  s2,
  output q0,
  output q1,
  output q2
);

  wire and_1_out, and_2_out, and_3_out, not_1_out, not_2_out, not_3_out, not_4_out;

  not not_1 (not_1_out, s0);
  not not_2 (not_2_out, s0);
  not not_3 (not_3_out, s0);
  not not_4 (not_4_out, s2);
  and and_1 (and_1_out, not_1_out, s2);
  and and_2 (and_2_out, not_2_out, s1);
  and and_3 (and_3_out, not_3_out, not_4_out);
  or or_1 (q0, and_1_out, and_2_out);
  or or_2 (q1, and_3_out, s1);

  assign q2 = s2;
endmodule
