// Logisim project 移位器.circ as structural Verilog: 2 circuits, main circuit main
module main (
  input  [7:0] in_1,
  input  [2:0] in_2,
  input  in_3,
  input  in_4,
  output [7:0] out_5,
  output [7:0] out_6,
  output [7:0] out_7
);

  wire [7:0] demultiplexer_1_out0, demultiplexer_1_out1, demultiplexer_2_out0, demultiplexer_2_out1,
       demultiplexer_3_out0, demultiplexer_3_out1;

  Demultiplexer #(.width(8)) demultiplexer_1 (
    .out0(demultiplexer_1_out0), .out1(demultiplexer_1_out1), .in(in_1), .sel(in_2[0]), .en(1'b1));
  Decoder #(.select(3)) decoder_1 ();  // open: out0, out1, out2, out3, out4, out5, out6, out7, sel, en
  assign out_5 = {demultiplexer_1_out1[6:0], demultiplexer_1_out1[7]} | demultiplexer_1_out0;  // OR_Gate or_1, 8 bits wide
  Demultiplexer #(.width(8)) demultiplexer_2 (
    .out0(demultiplexer_2_out0), .out1(demultiplexer_2_out1), .in(out_5), .sel(in_2[1]), .en(1'b1));
  Comparator #(.width(1), .mode("unsigned")) comparator_1 (.a(in_3), .b(in_4));  // open: gt, eq, lt
  assign out_6 = {demultiplexer_2_out1[5:0], demultiplexer_2_out1[7:6]} | demultiplexer_2_out0;  // OR_Gate or_2, 8 bits wide
  Demultiplexer #(.width(8)) demultiplexer_3 (
    .out0(demultiplexer_3_out0), .out1(demultiplexer_3_out1), .in(out_6), .sel(in_2[2]), .en(1'b1));
  assign out_7 = {demultiplexer_3_out1[3:0], demultiplexer_3_out1[7:4]} | demultiplexer_3_out0;  // OR_Gate or_3, 8 bits wide
endmodule

module mux (
  input  a,
  input  b,
  input  c,
  output s
);

  wire and_1_out, and_2_out, not_1_out;

  not not_1 (not_1_out, c);
  and and_1 (and_1_out, b, c);
  and and_2 (and_2_out, a, not_1_out);
  or or_1 (s, and_1_out, and_2_out);
endmodule
