// Logisim project XOR.circ as structural Verilog: 1 circuit, main circuit main
module main (
  input  in_1,
  input  NAND_GATE,
  input  in_3,
  input  in_4,
  input  in_5,
  input  in_6,
  input  in_7,
  input  in_8,
  input  in_9,
  input  AND_GATE,
  input  x,
  input  in_12,
  input  in_13,
  input  in_14,
  input  in_15,
  input  in_16,
  input  in_17,
  input  in_18,
  input  in_19,
  input  y,
  input  in_21,
  input  in_22,
  input  in_23,
  input  in_24,
  input  Even_Parity,
  input  in_26,
  input  in_27,
  input  in_28,
  input  in_29,
  input  in_30,
  input  in_31,
  input  in_32,
  input  in_33,
  input  in_34,
  input  in_35,
  input  in_36,
  input  in_37,
  input  in_38,
  input  in_39,
  output out_40,
  output out_41,
  output out_42,
  output out_43,
  output out_44,
  output out_45,
  output out_46,
  output out_47,
  output out_48,
  output out_49,
  output out_50,
  output out_51
);

  wire and_1_out, and_2_out, nor_1_out, not_2_out, not_3_out;

  assign out_42 = in_8 ? in_5 : 1'bz;  // Controlled_Buffer controlled_buffer_1
  assign out_45 = in_19 ? ~in_15 : 1'bz;  // Controlled_Inverter controlled_inverter_1
  or or_1 (out_49, in_27, in_32);
  nor nor_1 (nor_1_out, in_36, in_38);
  LED led_1 (.in(nor_1_out));
  not not_1 (out_40, in_1);
  buf buffer_1 (out_43, in_6);
  not not_2 (not_2_out, x);
  not not_3 (not_3_out, y);
  and and_1 (and_1_out, not_2_out, y);
  and and_2 (and_2_out, x, not_3_out);
  or or_2 (out_46, and_1_out, and_2_out);
  ExactlyOne xor_1 (.out(out_48), .in0(in_24), .in1(in_26), .in2(in_29), .in3(in_31), .in4(in_34));
  xnor xnor_1 (out_51, in_37, in_39);
  nand nand_1 (out_41, NAND_GATE, in_3, in_4, in_7, in_9);
  and and_3 (out_44, AND_GATE, in_12, in_13, in_14, in_16);
  xor odd_parity_1 (out_47, in_17, in_18, in_21, in_22, in_23);
  xnor even_parity_1 (out_50, Even_Parity, in_28, in_30, in_33, in_35);

  // Notes on the sheet:
  //   Controlled Buffer
  //   Controlled Inverter
  //   OR GATE
  //   NOR GATE
  //   NOT GATE
  //   Buffer
  //   XOR Circuit built using Logisim
  //   XOR GATE
  //   XNOR GATE
  //   Odd Parity
endmodule
