// Logisim project practice.circ as structural Verilog: 1 circuit, main circuit main
module main (
  input  in_1,
  input  in_2,
  input  in_3,
  input  [5:0] in_4,
  output out_5,
  output out_6,
  output [2:0] out_7
);

  wire and_1_out, and_2_out, xor_1_out;

  // Probe on in_1
  xor xor_1 (xor_1_out, in_1, in_2);
  xor xor_2 (out_5, xor_1_out, in_3);
  and and_1 (and_1_out, in_3, xor_1_out);
  and and_2 (and_2_out, in_1, in_2);
  assign out_7 = ~(in_4[2:0] ^ in_4[5:3]);  // XNOR_Gate xnor_1, 3 bits wide
  or or_1 (out_6, and_1_out, and_2_out);
endmodule
