// Logisim project swap.circ as structural Verilog: 1 circuit, main circuit swap
module swap (
  input  I1,
  input  I2,
  input  s,
  output _01,
  output _02
);

  wire and_1_out, and_2_out, and_3_out, and_4_out, not_1_out, not_2_out;

  not not_1 (not_1_out, s);
  not not_2 (not_2_out, s);
  and and_1 (and_1_out, I2, not_2_out);
  and and_2 (and_2_out, I1, not_1_out);
  and and_3 (and_3_out, s, I2);
  and and_4 (and_4_out, I1, s);
  or or_1 (_01, and_2_out, and_3_out);
  or or_2 (_02, and_4_out, and_1_out);
endmodule
