// Logisim project work.circ as structural Verilog
module full_adder (
  input  a,
  input  b,
  input  carry,
  output sum,
  output carry_2
);

  wire and_1_out, and_2_out, and_3_out, and_4_out, and_5_out, and_6_out, and_7_out, not_1_out, not_2_out,
       not_3_out, not_4_out, not_5_out, not_6_out;

  not not_1 (not_1_out, a);
  not not_2 (not_2_out, b);
  not not_3 (not_3_out, a);
  not not_4 (not_4_out, carry);
  not not_5 (not_5_out, b);
  not not_6 (not_6_out, carry);
  and and_1 (and_1_out, b, carry);
  and and_2 (and_2_out, a, carry);
  and and_3 (and_3_out, a, b);
  and and_4 (and_4_out, not_1_out, not_2_out, carry);
  and and_5 (and_5_out, not_3_out, b, not_4_out);
  and and_6 (and_6_out, a, not_5_out, not_6_out);
  and and_7 (and_7_out, a, b, carry);
  or or_1 (carry_2, and_1_out, and_2_out, and_3_out);
  or or_2 (sum, and_4_out, and_5_out, and_6_out, and_7_out);
endmodule

module pre (
  input  A,
  input  B,
  input  C,
  input  A_2,
  input  B_2,
  input  C_2,
  input  in_7,
  input  in_8,
  input  in_9,
  output Y,
  output Y_2,
  output out_12
);

  wire and_1_out, and_2_out, and_3_out, and_4_out, and_5_out, and_6_out, not_1_out, not_2_out, not_3_out,
       not_4_out, not_5_out, not_6_out, or_2_out, or_3_out;

  not not_1 (not_1_out, C);
  and and_1 (and_1_out, B, C);
  and and_2 (and_2_out, A, not_1_out);
  not not_2 (not_2_out, C_2);
  not not_3 (not_3_out, B_2);
  not not_4 (not_4_out, C_2);
  not not_5 (not_5_out, A_2);
  not not_6 (not_6_out, in_9);
  or or_1 (Y, and_1_out, and_2_out);
  or or_2 (or_2_out, in_7, in_9);
  or or_3 (or_3_out, in_8, not_6_out);
  and and_3 (and_3_out, not_2_out, not_3_out, A_2);
  and and_4 (and_4_out, not_4_out, B_2, A_2);
  and and_5 (and_5_out, C_2, B_2, not_5_out);
  and and_6 (and_6_out, C_2, B_2, A_2);
  and and_7 (out_12, or_2_out, or_3_out);
  or or_4 (Y_2, and_3_out, and_4_out, and_5_out, and_6_out);
endmodule

module qu (
  input  A,
  input  B,
  input  C,
  output _01,
  output _02
);

  wire and_1_out, and_2_out, and_3_out, and_4_out, not_1_out, not_2_out;

  not not_1 (not_1_out, C);
  not not_2 (not_2_out, C);
  and and_1 (and_1_out, B, C);
  and and_2 (and_2_out, A, not_1_out);
  and and_3 (and_3_out, B, not_2_out);
  and and_4 (and_4_out, A, C);
  or or_1 (_01, and_1_out, and_2_out);
  or or_2 (_02, and_3_out, and_4_out);
endmodule

module pre2 (
  input  A,
  input  B,
  input  C,
  output out_4
);

  wire and_1_out, and_2_out, not_1_out, not_2_out, not_3_out, not_4_out, not_5_out, not_6_out, or_1_out,
       or_2_out;

  not not_1 (not_1_out, A);
  not not_2 (not_2_out, B);
  not not_3 (not_3_out, A);
  not not_4 (not_4_out, A);
  or or_1 (or_1_out, C, B, not_1_out);
  or or_2 (or_2_out, C, not_2_out, not_3_out);
  not not_5 (not_5_out, or_2_out);
  and and_1 (and_1_out, C, B, not_4_out);
  and and_2 (and_2_out, C, B, A);
  not not_6 (not_6_out, or_1_out);
  or or_3 (out_4, not_6_out, not_5_out, and_1_out, and_2_out);
endmodule
